// Logisim project ex2.circ as structural Verilog: 6 circuits, main circuit AND2
module AND2 (
  input  A,
  input  B,
  output RESULT
);

  and and_1 (RESULT, A, B);

  // Notes on the sheet:
  //   Sample Circuit
endmodule

module NAND2 (
  input  A,
  input  B,
  output RESULT
);

  wire and_1_out;

  and and_1 (and_1_out, A, B);
  not not_1 (RESULT, and_1_out);
endmodule

module NOR2 (
  input  A,
  input  B,
  output RESULT
);

  wire or_1_out;

  or or_1 (or_1_out, A, B);
  not not_1 (RESULT, or_1_out);
endmodule

module XOR2 (
  input  A,
  input  B,
  output RESULT
);

  wire nand2_1_result, or_1_out;

  or or_1 (or_1_out, A, B);
  and and_1 (RESULT, or_1_out, nand2_1_result);
  NAND2 nand2_1 (.A(A), .B(B), .RESULT(nand2_1_result));
endmodule

module MUX2 (
  input  A,
  input  B,
  input  SEL,
  output RESULT
);

  wire and_1_out, and_2_out, not_1_out;

  not not_1 (not_1_out, SEL);
  and and_1 (and_1_out, A, not_1_out);
  and and_2 (and_2_out, B, SEL);
  or or_1 (RESULT, and_1_out, and_2_out);
endmodule

module MUX4 (
  input  A,
  input  B,
  input  C,
  input  D,
  input  SEL0,
  input  SEL1,
  output RESULT
);

  wire nor2_1_result;

  NOR2 nor2_1 (.A(SEL0), .B(SEL1), .RESULT(nor2_1_result));
  MUX2 mux2_1 (.A(A), .SEL(nor2_1_result), .RESULT(RESULT));  // open: B
  MUX2 mux2_2 ();  // open: A, B, SEL, RESULT
  MUX2 mux2_3 ();  // open: A, B, SEL, RESULT
  MUX2 mux2_4 ();  // open: A, B, SEL, RESULT
endmodule
