// Logisim project control-logic.circ as structural Verilog: 1 circuit, main circuit control_logic
module control_logic (
  input  [31:0] Instruction,
  input  BrEq,
  input  BrLt,
  output PCSel,
  output RegWEn,
  output [2:0] ImmSel,
  output BrUn,
  output ASel,
  output BSel,
  output [3:0] ALUSel,
  output MemWEn,
  output [1:0] WBSel
);

  wire comparator_3_eq, comparator_4_eq, comparator_5_eq, IsAdd, IsAddi, IsAnd, IsAndi, IsMul, IsMulh,
       IsMulhu, IsOr, IsOri, IsSll, IsSlli, IsSlt, IsSlti, IsSra, IsSrai, IsSrl, IsSrli, IsSub, IsXor,
       IsXori, IType, RType;
  wire [1:0] priority_encoder_1_out;
  wire [5:0] ITypeInstruction, multiplexer_1_out, multiplexer_2_out, multiplexer_3_out, multiplexer_4_out,
       RomInput, RTypeInstruction;
  wire [15:14] rom_1_data;

  ROM #(.addrWidth(6), .dataWidth(16)) rom_1 (
    .addr(RomInput), .data({rom_1_data, WBSel, MemWEn, ALUSel, BSel, ASel, BrUn, ImmSel, RegWEn}));
  Comparator #(.width(7)) comparator_1 (.a(Instruction[6:0]), .b(7'b0010011), .eq(IType));  // open: gt, lt
  Comparator #(.width(7)) comparator_2 (.a(Instruction[6:0]), .b(7'b0110011), .eq(RType));  // open: gt, lt
  Comparator #(.width(7)) comparator_3 (.a(Instruction[31:25]), .b({7{1'b0}}), .eq(comparator_3_eq));  // open: gt, lt
  Comparator #(.width(7)) comparator_4 (.a(Instruction[31:25]), .b(7'b0000001), .eq(comparator_4_eq));  // open: gt, lt
  Comparator #(.width(7)) comparator_5 (.a(Instruction[31:25]), .b(7'b0100000), .eq(comparator_5_eq));  // open: gt, lt
  Multiplexer #(.enable("true"), .width(6)) multiplexer_1 (
    .in0(6'b010011), .in1(6'b010100), .out(multiplexer_1_out), .sel(Instruction[30]), .en(IType));
  Priority_Encoder #(.select_enc(2)) priority_encoder_1 (
    .in0(comparator_3_eq), .in1(comparator_4_eq), .in2(comparator_5_eq), .in3(1'b0),
    .out(priority_encoder_1_out));  // open: gs, en_out, en_in
  Multiplexer #(.enable("true"), .width(6)) multiplexer_2 (
    .in0(6'b000011), .in1(6'b000100), .out(multiplexer_2_out), .sel(Instruction[25]), .en(RType));
  Multiplexer #(.enable("true"), .width(6)) multiplexer_3 (
    .in0(6'b001000), .in1(6'b001001), .out(multiplexer_3_out), .sel(Instruction[30]), .en(RType));
  Multiplexer #(.enable("true"), .select(2), .width(6)) multiplexer_4 (
    .in0({6{1'b0}}), .in1(6'b000001), .in2(6'b000010), .in3({6{1'b1}}), .out(multiplexer_4_out),
    .sel(priority_encoder_1_out), .en(RType));
  Multiplexer #(.enable("true"), .select(3), .width(6)) multiplexer_5 (
    .in0(6'b001111), .in1(6'b010000), .in2(6'b010001), .in3({6{1'b0}}), .in4(6'b010010),
    .in5(multiplexer_1_out), .in6(6'b010101), .in7(6'b010110), .out(ITypeInstruction),
    .sel(Instruction[14:12]), .en(IType));
  Multiplexer #(.enable("true"), .select(3), .width(6)) multiplexer_6 (
    .in0(multiplexer_4_out), .in1(multiplexer_2_out), .in2(6'b000110), .in3(6'b000101), .in4(6'b000111),
    .in5(multiplexer_3_out), .in6(6'b001010), .in7(6'b001011), .out(RTypeInstruction),
    .sel(Instruction[14:12]), .en(RType));
  Priority_Encoder #(.select_enc(6)) priority_encoder_2 (
    .in0(IsAdd), .in1(IsMul), .in2(IsSub), .in3(IsSll), .in4(IsMulh), .in5(IsMulhu), .in6(IsSlt),
    .in7(IsXor), .in8(IsSrl), .in9(IsSra), .in10(IsOr), .in11(IsAnd), .in15(IsAddi), .in16(IsSlli),
    .in17(IsSlti), .in18(IsXori), .in19(IsSrli), .in20(IsSrai), .in21(IsOri), .in22(IsAndi), .out(RomInput));  // open: in12, in13, in14, in23, in24, in25, in26, in27, in28, in29, in30, in31, in32, in33, in34, in35, in36, in37, in38, in39, in40, in41, in42, in43, in44, in45, in46, in47, in48, in49, in50, in51, in52, in53, in54, in55, in56, in57, in58, in59, in60, in61, in62, in63, gs, en_out, en_in
  Comparator #(.width(6)) comparator_6 (.a(ITypeInstruction), .b(6'b001111), .eq(IsAddi));  // open: gt, lt
  Comparator #(.width(6)) comparator_7 (.a(ITypeInstruction), .b(6'b010000), .eq(IsSlli));  // open: gt, lt
  Comparator #(.width(6)) comparator_8 (.a(ITypeInstruction), .b(6'b010001), .eq(IsSlti));  // open: gt, lt
  Comparator #(.width(6)) comparator_9 (.a(ITypeInstruction), .b(6'b010010), .eq(IsXori));  // open: gt, lt
  Comparator #(.width(6)) comparator_10 (.a(ITypeInstruction), .b(6'b010011), .eq(IsSrli));  // open: gt, lt
  Comparator #(.width(6)) comparator_11 (.a(ITypeInstruction), .b(6'b010100), .eq(IsSrai));  // open: gt, lt
  Comparator #(.width(6)) comparator_12 (.a(ITypeInstruction), .b(6'b010101), .eq(IsOri));  // open: gt, lt
  Comparator #(.width(6)) comparator_13 (.a(ITypeInstruction), .b(6'b010110), .eq(IsAndi));  // open: gt, lt
  Comparator #(.width(6)) comparator_14 (.a(RTypeInstruction), .b({6{1'b0}}), .eq(IsAdd));  // open: gt, lt
  Comparator #(.width(6)) comparator_15 (.a(RTypeInstruction), .b(6'b000001), .eq(IsMul));  // open: gt, lt
  Comparator #(.width(6)) comparator_16 (.a(RTypeInstruction), .b(6'b000010), .eq(IsSub));  // open: gt, lt
  Comparator #(.width(6)) comparator_17 (.a(RTypeInstruction), .b(6'b000011), .eq(IsSll));  // open: gt, lt
  Comparator #(.width(6)) comparator_18 (.a(RTypeInstruction), .b(6'b000100), .eq(IsMulh));  // open: gt, lt
  Comparator #(.width(6)) comparator_19 (.a(RTypeInstruction), .b(6'b000101), .eq(IsMulhu));  // open: gt, lt
  Comparator #(.width(6)) comparator_20 (.a(RTypeInstruction), .b(6'b000110), .eq(IsSlt));  // open: gt, lt
  Comparator #(.width(6)) comparator_21 (.a(RTypeInstruction), .b(6'b000111), .eq(IsXor));  // open: gt, lt
  Comparator #(.width(6)) comparator_22 (.a(RTypeInstruction), .b(6'b001000), .eq(IsSrl));  // open: gt, lt
  Comparator #(.width(6)) comparator_23 (.a(RTypeInstruction), .b(6'b001001), .eq(IsSra));  // open: gt, lt
  Comparator #(.width(6)) comparator_24 (.a(RTypeInstruction), .b(6'b001010), .eq(IsOr));  // open: gt, lt
  Comparator #(.width(6)) comparator_25 (.a(RTypeInstruction), .b(6'b001011), .eq(IsAnd));  // open: gt, lt

  assign PCSel = 1'b0;

  // Other names for the same wires on the sheet: ITypeFun3[2:0] = Instruction[14:12];
  //   RTypeFun3[2:0] = Instruction[14:12]; ITypeFun7[6:0] = Instruction[31:25]; RTypeFun7[6:0] = Instruction[31:25]

  // Notes on the sheet:
  //   INPUTS to your circuit
  //   Connect ROM Input here ->
  //   contents of rom_1 (hex, n*v repeats v):
  //   100f 140f 160f 109f 148f 159f 110f 121f 129f 168f 131f 139f 0 0 0 1041 10d1 1141 1251 12d1 16c1 1351
  //   13d1
  //   ROM FOR CONTROL LOGIC
  //   DON'T CHANGE THE LOCATIONS OF THE INPUTS AND OUTPUTS!
  //   This is only if you choose to do the ROM option
  //   CONNECT
  //   WIRE
  //   TO
  //   USE
  //   ROM
  //   OUTPUT from your circuit
  //   Reminder: If using ROM, use combinational logic for PCSel
endmodule
