// Logisim project cpu.circ as structural Verilog: 1 circuit, main circuit cpu
module cpu (
  input  clk,
  input  [31:0] Instruction,
  input  [31:0] MemReadData,
  output [31:0] MemAddress,
  output [31:0] ProgramCounter,
  output [31:0] ra,
  output [31:0] sp,
  output [31:0] t0,
  output [31:0] t1,
  output [31:0] t2,
  output [31:0] s0,
  output [31:0] s1,
  output [31:0] a0,
  output [3:0] MemWriteMask,
  output [31:0] MemWriteData
);

  wire ASel, BrEq, BrLt, BrUn, BSel, MemWEn, partial_store_1_p1, partial_store_1_p2, partial_store_1_p4,
       partial_store_1_p6, PCSel, regfile_1_p7, regfile_1_p8, regfile_1_p10, regfile_1_p22, regfile_1_p24,
       RegWEn;
  wire [1:0] WBSel;
  wire [2:0] ImmSel;
  wire [3:0] ALUSel;
  wire [31:0] adder_1_out, ALUResult, DEMEResult, imm, multiplexer_1_out, multiplexer_2_out,
       multiplexer_3_out, PCPulsFour, ReadData1, ReadData2;

  Register #(.width(32)) PC (.D(adder_1_out), .clk(clk), .Q(ProgramCounter));  // open: en, clr
  Adder #(.width(32)) adder_1 (.a(ProgramCounter), .b(32'h4), .out(adder_1_out));  // open: cin, cout
  Multiplexer #(.select(2), .width(32)) multiplexer_1 (
    .in0({32{1'b1}}), .in1(ALUResult), .in2(DEMEResult), .in3(PCPulsFour), .out(multiplexer_1_out),
    .sel(WBSel));
  control_logic control_logic_1 (
    .Instruction(Instruction), .BrEq(BrEq), .BrLt(BrLt), .PCSel(PCSel), .RegWEn(RegWEn), .ImmSel(ImmSel),
    .BrUn(BrUn), .ASel(ASel), .BSel(BSel), .ALUSel(ALUSel), .MemWEn(MemWEn), .WBSel(WBSel));
  // regfile regfile_1: pin names not known; wires that end beside it: Instruction[19:15], Instruction[24:20], Instruction[11:7], multiplexer_1_out, RegWEn, clk, regfile_1_p7, regfile_1_p8, regfile_1_p8, regfile_1_p10, ra, sp, t0, t1, t2, s0, s1, a0, ReadData1, ReadData2, regfile_1_p10, regfile_1_p22, regfile_1_p22, regfile_1_p24, regfile_1_p24
  imm_gen imm_gen_1 (.Instruction(Instruction), .ImmSel(ImmSel), .Immediate(imm));
  Multiplexer #(.width(32)) multiplexer_2 (.in0(ReadData1), .in1(ProgramCounter), .out(multiplexer_2_out), .sel(ASel));
  Multiplexer #(.width(32)) multiplexer_3 (.in0(ReadData2), .in1(imm), .out(multiplexer_3_out), .sel(BSel));
  // alu alu_1: pin names not known; wires that end beside it: multiplexer_2_out, multiplexer_3_out, ALUSel, ALUResult
  // branch_comp branch_comp_1: pin names not known
  // partial_store partial_store_1: pin names not known; wires that end beside it: partial_store_1_p1, partial_store_1_p2, partial_store_1_p2, partial_store_1_p4, partial_store_1_p4, partial_store_1_p6, partial_store_1_p1, partial_store_1_p6
  // partial_load partial_load_1: pin names not known

  // Notes on the sheet:
  //   To IMEM
  //   IMEM (do **NOT** move this)
  //   From IMEM
  //   Inputs/Outputs for testing. Do **NOT** move these.
  //   It is OK to move the PC, RegFile, ALU, MEM, Branch Comp, Imm Gen, Partial Load, Partial Store and Control Logic to wherever is most convenient for you when constructing your CPU, and to delete this text
  //   To DMEM
  //   DMEM (do **NOT** move this)
  //   From DMEM
endmodule
